// Digital circuit jm_control_matrix_p127.dig as structural Verilog
module jm_control_matrix_p127 (
  input  T5,
  input  T4,
  input  T3,
  input  T2,
  input  T1,
  input  LDA,
  input  ADD,
  input  SUB,
  input  OUT,
  input  T6
);

  wire nand_1_out, nand_2_out, nand_3_out, nand_4_out, nand_5_out, nand_6_out, nand_7_out, nand_8_out,
       nand_9_out, nand_10_out, nand_11_out, nand_12_out, nand_13_out, nand_14_out, nand_15_out, nand_16_out,
       nand_17_out, nand_18_out, nand_19_out, nand_20_out, nand_21_out, nand_22_out, nand_23_out,
       nand_24_out, nand_25_out, not_1_out, not_2_out, not_3_out, not_4_out, not_5_out, not_6_out, not_7_out,
       not_8_out, not_9_out, not_10_out;

  not not_1 (not_1_out, T1);
  LED Cp (.in(T2));
  LED Ep (.in(not_1_out));
  nand nand_1 (nand_1_out, T4, LDA);
  nand nand_2 (nand_2_out, T4, ADD);
  nand nand_3 (nand_3_out, nand_4_out, nand_2_out, nand_1_out, not_1_out);
  not not_2 (not_2_out, nand_3_out);
  LED Lm (.in(not_2_out));
  nand nand_4 (nand_4_out, T4, SUB);
  not not_3 (not_3_out, T3);
  nand nand_5 (nand_5_out, T5, LDA);
  not not_4 (not_4_out, nand_7_out);
  LED CE (.in(not_4_out));
  nand nand_6 (nand_6_out, T5, ADD);
  nand nand_7 (nand_7_out, nand_8_out, nand_6_out, nand_5_out, not_3_out);
  nand nand_8 (nand_8_out, T5, SUB);
  not not_5 (not_5_out, T3);
  LED Li (.in(not_5_out));
  nand nand_9 (nand_9_out, T4, LDA);
  nand nand_10 (nand_10_out, T4, ADD);
  nand nand_11 (nand_11_out, nand_12_out, nand_10_out, nand_9_out);
  not not_6 (not_6_out, nand_11_out);
  LED Ei (.in(not_6_out));
  nand nand_12 (nand_12_out, T4, SUB);
  nand nand_13 (nand_13_out, T5, LDA);
  nand nand_14 (nand_14_out, T6, ADD);
  nand nand_15 (nand_15_out, nand_16_out, nand_14_out, nand_13_out);
  not not_7 (not_7_out, nand_15_out);
  LED La (.in(not_7_out));
  nand nand_16 (nand_16_out, T6, SUB);
  LED Ea (.in(nand_17_out));
  nand nand_17 (nand_17_out, T4, OUT);
  nand nand_18 (nand_18_out, T6, SUB);
  not not_8 (not_8_out, nand_18_out);
  LED Su (.in(not_8_out));
  nand nand_19 (nand_19_out, T6, ADD);
  not not_9 (not_9_out, nand_21_out);
  LED Eu (.in(not_9_out));
  nand nand_20 (nand_20_out, T6, SUB);
  nand nand_21 (nand_21_out, nand_20_out, nand_19_out);
  nand nand_22 (nand_22_out, T5, ADD);
  nand nand_23 (nand_23_out, T5, SUB);
  nand nand_24 (nand_24_out, nand_23_out, nand_22_out);
  not not_10 (not_10_out, nand_24_out);
  LED Lb (.in(not_10_out));
  LED Lo (.in(nand_25_out));
  nand nand_25 (nand_25_out, T4, OUT);
endmodule
