// Digital circuit jm_control_matrix_p212_5cycle.dig as structural Verilog
module jm_control_matrix_p212_5cycle (
  input  T5,
  input  T4,
  input  T3,
  input  T2,
  input  T1,
  input  LDA,
  input  ADD,
  input  SUB,
  input  OUT,
  input  JMP,
  input  JZ,
  input  JNZ,
  input  JC,
  input  JNC,
  input  Z,
  input  C
);

  wire nand_1_out, nand_2_out, nand_3_out, nand_4_out, nand_5_out, nand_6_out, nand_7_out, nand_8_out,
       nand_9_out, nand_10_out, nand_11_out, nand_12_out, nand_13_out, nand_14_out, nand_15_out, nand_16_out,
       nand_17_out, nand_18_out, nand_19_out, nand_20_out, nand_21_out, nand_22_out, nand_23_out,
       nand_24_out, nand_25_out, nand_26_out, nand_27_out, nand_28_out, nand_29_out, nand_30_out,
       nand_31_out, nand_32_out, nand_33_out, nand_34_out, nand_35_out, nand_36_out, not_1_out, not_2_out,
       not_3_out, not_4_out, not_5_out, not_6_out, not_7_out, not_8_out, not_9_out, not_10_out, not_11_out,
       not_12_out, not_13_out, not_14_out, not_15_out, not_16_out, not_17_out, not_18_out, not_19_out,
       not_20_out, not_21_out, not_22_out, not_23_out, not_24_out;

  not not_1 (not_1_out, T1);
  not not_2 (not_2_out, not_1_out);
  LED Cp (.in(T2));
  LED Ep (.in(not_2_out));
  nand nand_1 (nand_1_out, T3, LDA);
  nand nand_2 (nand_2_out, T3, ADD);
  nand nand_3 (nand_3_out, nand_4_out, nand_2_out, nand_1_out, not_1_out);
  not not_3 (not_3_out, nand_3_out);
  not not_4 (not_4_out, not_3_out);
  LED Lm (.in(not_4_out));
  nand nand_4 (nand_4_out, T3, SUB);
  not not_5 (not_5_out, T2);
  nand nand_5 (nand_5_out, T4, LDA);
  not not_6 (not_6_out, nand_7_out);
  not not_7 (not_7_out, not_6_out);
  LED CE (.in(not_7_out));
  nand nand_6 (nand_6_out, T4, ADD);
  nand nand_7 (nand_7_out, nand_8_out, nand_6_out, nand_5_out, not_5_out);
  nand nand_8 (nand_8_out, T4, SUB);
  not not_8 (not_8_out, T2);
  not not_9 (not_9_out, not_8_out);
  LED Li (.in(not_9_out));
  nand nand_9 (nand_9_out, T3, LDA);
  nand nand_10 (nand_10_out, T3, ADD);
  nand nand_11 (nand_11_out, T3, SUB);
  nand nand_12 (nand_12_out, JMP, T3);
  not not_10 (not_10_out, nand_14_out);
  not not_11 (not_11_out, not_10_out);
  LED Ei (.in(not_11_out));
  nand nand_13 (nand_13_out, JZ, T3);
  nand nand_14 (nand_14_out, nand_17_out, nand_16_out, nand_15_out, nand_13_out, nand_12_out, nand_11_out, nand_10_out, nand_9_out);
  nand nand_15 (nand_15_out, T3, JNZ);
  nand nand_16 (nand_16_out, T3, JC);
  nand nand_17 (nand_17_out, T3, JNC);
  nand nand_18 (nand_18_out, T4, LDA);
  nand nand_19 (nand_19_out, T5, ADD);
  nand nand_20 (nand_20_out, nand_21_out, nand_19_out, nand_18_out);
  not not_12 (not_12_out, nand_20_out);
  not not_13 (not_13_out, not_12_out);
  LED La (.in(not_13_out));
  nand nand_21 (nand_21_out, T5, SUB);
  not not_14 (not_14_out, nand_22_out);
  LED Ea (.in(not_14_out));
  nand nand_22 (nand_22_out, T3, OUT);
  nand nand_23 (nand_23_out, T5, SUB);
  not not_15 (not_15_out, nand_23_out);
  LED Su (.in(not_15_out));
  nand nand_24 (nand_24_out, T5, ADD);
  not not_16 (not_16_out, nand_26_out);
  not not_17 (not_17_out, not_16_out);
  LED Eu (.in(not_17_out));
  nand nand_25 (nand_25_out, T5, SUB);
  nand nand_26 (nand_26_out, nand_25_out, nand_24_out);
  nand nand_27 (nand_27_out, T4, ADD);
  nand nand_28 (nand_28_out, T4, SUB);
  nand nand_29 (nand_29_out, nand_28_out, nand_27_out);
  not not_18 (not_18_out, nand_29_out);
  not not_19 (not_19_out, not_18_out);
  LED Lb (.in(not_19_out));
  not not_20 (not_20_out, nand_30_out);
  LED Lo (.in(not_20_out));
  nand nand_30 (nand_30_out, T3, OUT);
  nand nand_31 (nand_31_out, Z, T3, JZ);
  not not_21 (not_21_out, Z);
  nand nand_32 (nand_32_out, T3, not_21_out, JNZ);
  nand nand_33 (nand_33_out, T3, C, JC);
  nand nand_34 (nand_34_out, nand_36_out, nand_35_out, nand_33_out, nand_32_out, nand_31_out);
  not not_22 (not_22_out, nand_34_out);
  not not_23 (not_23_out, not_22_out);
  LED Lp (.in(not_23_out));
  not not_24 (not_24_out, C);
  nand nand_35 (nand_35_out, T3, not_24_out, JNC);
  nand nand_36 (nand_36_out, T3, JMP);
endmodule
